# Fritzing sketch tp7-montage (saved by Fritzing 0.9.4)
breadboards: 1

parts:
  part = WeMos D1 Mini
  LED1 = LED - 5mm [color="Red (633nm)" package="5 mm [THT]"]
  R1 = Photocell (LDR) [package=THT]
  LED3 = LED - 5mm [color="Green (570nm)" package="5 mm [THT]"]
  R2 = Resistor [tolerance=±5% resistance=3.3k package=THT]
  R4 = Resistor [tolerance=±5% resistance=220 package=THT]
  LED2 = LED - 5mm [color="Orange (620nm)" package="5 mm [THT]"]
  R5 = Resistor [tolerance=±5% resistance=220 package=THT]
  R6 = Resistor [tolerance=±5% resistance=220 package=THT]

nets:
  N1: part.D0, R6.Pin_0
  N2: part.D5, R5.Pin_0
  N3: part.D6, R4.Pin_0
  N4: LED1.cathode, LED3.cathode, R2.Pin_0, LED2.cathode
  N5: LED1.anode, R6.Pin_1
  N6: R1.pin_1, R2.Pin_1
  N7: LED3.anode, R4.Pin_1
  N8: LED2.anode, R5.Pin_1
