# Fritzing sketch tp8.2-montage (saved by Fritzing 0.9.4)
breadboards: 1

parts:
  part = WeMos D1 Mini
  LED1 = LED - 5mm [color="Red (633nm)" package="5 mm [THT]"]
  LED3 = LED - 5mm [color="Green (570nm)" package="5 mm [THT]"]
  R4 = Resistor [tolerance=±5% resistance=220 package=THT]
  LED2 = LED - 5mm [color="Orange (620nm)" package="5 mm [THT]"]
  R5 = Resistor [tolerance=±5% resistance=220 package=THT]
  R6 = Resistor [tolerance=±5% resistance=220 package=THT]
  part_2 = HC-SR04 Ultrasonic Distance Sensor

nets:
  N1: part.D0, R6.Pin_0
  N2: part.D1, part_2.ECHO
  N3: part.D2, part_2.TRIG
  N4: part.D5, R5.Pin_0
  N5: part.D6, R4.Pin_0
  GND: LED1.cathode, LED3.cathode, LED2.cathode, part_2.GND
  N6: LED1.anode, R6.Pin_1
  N7: LED3.anode, R4.Pin_1
  N8: LED2.anode, R5.Pin_1
  5V: part_2.VCC

custom parts:
  HC-SR04 Ultrasonic Distance Sensor: The HC-SR04 is an ultrasonic distance sensor. It is capable of providing measurement for ranges of 2cm to 400cm. The module operates at 5V.
